# Fritzing sketch control (saved by Fritzing 0.9.3b)
breadboards: 1

parts:
  Part2 = Arduino Nano (Rev3.0)
  ENC28J1 = ENC28J60
  OLED1 = 128x64 Monochrom OLED Display with SPI Control
  U1 = 74HC165 [part_number=SN74LS165 package="DIP16 [THT]"]
  U1_2 = SLIDER [package=slider]
  U2 = SLIDER [package=slider]
  S0 = Momentary Switch [package=ksa_sealed_tac_switch]
  R0 = Resistor [tolerance=±5% resistance=220 package="0603 [SMD]"]
  S1 = Momentary Switch [package=ksa_sealed_tac_switch]
  R1 = Resistor [tolerance=±5% resistance=220 package="0603 [SMD]"]
  S2 = Momentary Switch [package=ksa_sealed_tac_switch]
  R2 = Resistor [tolerance=±5% resistance=220 package="0603 [SMD]"]
  S3 = Momentary Switch [package=ksa_sealed_tac_switch]
  R3 = Resistor [tolerance=±5% resistance=220 package="0603 [SMD]"]
  S4 = Momentary Switch [package=ksa_sealed_tac_switch]
  S5 = Momentary Switch [package=ksa_sealed_tac_switch]
  S6 = Momentary Switch [package=ksa_sealed_tac_switch]
  S7 = Momentary Switch [package=ksa_sealed_tac_switch]
  R4 = Resistor [tolerance=±5% resistance=220 package="0603 [SMD]"]
  R5 = Resistor [tolerance=±5% resistance=220 package="0603 [SMD]"]
  R6 = Resistor [tolerance=±5% resistance=220 package="0603 [SMD]"]
  R7 = Resistor [tolerance=±5% resistance=220 package="0603 [SMD]"]
  S8 = Momentary Switch [package=ksa_sealed_tac_switch]
  S9 = Momentary Switch [package=ksa_sealed_tac_switch]

nets:
  N1: Part2.RESET, Part2.D13/SCK, ENC28J1.SCK, ENC28J1.RST, OLED1.Clock
  N2: Part2.D2, U1.Q1
  N3: Part2.D3, U1.Q0
  N4: Part2.D5, U1.Q2
  N5: Part2.D7, OLED1.SA0/DC
  N6: Part2.D8, OLED1.Reset
  N7: Part2.D9, OLED1.CS
  N8: Part2.D10, ENC28J1.CS
  N9: Part2.D11/MOSI, ENC28J1.SI, OLED1.Data
  N10: Part2.D12/MISO, ENC28J1.SO
  N11: Part2.A3, S9.1
  N12: Part2.A2, S8.1
  N13: Part2.A1, U2.S
  N14: Part2.A0, U1_2.S
  3.3V: ENC28J1.3.3, OLED1.3v3
  GND: ENC28J1.GND, OLED1.GND, U1.GND, U1_2.A, U2.A, R0.Pin_1, R1.Pin_1, R2.Pin_1, R3.Pin_1, R4.Pin_1, R5.Pin_1, R6.Pin_1, R7.Pin_1, S8.4, S9.4
  N15: U1.Q3, S7.4, R7.Pin_0
  N16: U1.Q4, S6.4, R6.Pin_0
  N17: U1.Q5, S5.4, R5.Pin_0
  N18: U1.Q6, S4.4, R4.Pin_0
  N19: U1.SH_CP, S0.3, S0.4, R0.Pin_0
  N20: U1.ST_CP, S1.4, R1.Pin_0
  N21: U1.OE, S2.4, R2.Pin_0
  N22: U1.DS, S3.4, R3.Pin_0
  5V: U1.VCC, U1_2.E, U2.E, S3.1, S7.2
  N23: S0.1, S0.2, S1.2
  N24: S1.1, S2.2
  N25: S2.1, S3.2
  N26: S4.2, S5.1
  N27: S5.2, S6.1
  N28: S6.2, S7.1

custom parts:
  ENC28J60: Ethernet Module ENC28J60
  74HC165: 8-bit parallel-load shift registers
